// Logisim project sketch.circ as structural Verilog
module main (
  input  [7:0] in_1,
  input  [7:0] in_2,
  input  in_3,
  output [7:0] out_4
);

  wire clock_1_out, not_1_out;

  RAM ram_1 (.addr(in_1), .data(out_4), .clk(clock_1_out), .ld(in_3));  // open: sel, clr
  Clock clock_1 (.out(clock_1_out));
  not not_1 (not_1_out, in_3);
  assign out_4 = not_1_out ? in_2 : 8'bz;  // Controlled_Buffer controlled_buffer_1
endmodule

module Regs (
);

  wire undriven_2, undriven_4;
  wire [2:0] undriven_3, undriven_5;
  wire [7:0] demultiplexer_1_out0, demultiplexer_1_out1, demultiplexer_1_out2, demultiplexer_1_out3,
       demultiplexer_1_out4, demultiplexer_1_out5, demultiplexer_1_out6, demultiplexer_1_out7,
       multiplexer_1_out, register_1_q, register_2_q, register_3_q, register_4_q, register_5_q, register_6_q,
       register_7_q, register_8_q, undriven;

  Demultiplexer #(.select(3), .width(8)) demultiplexer_1 (
    .out0(demultiplexer_1_out0), .out1(demultiplexer_1_out1), .out2(demultiplexer_1_out2),
    .out3(demultiplexer_1_out3), .out4(demultiplexer_1_out4), .out5(demultiplexer_1_out5),
    .out6(demultiplexer_1_out6), .out7(demultiplexer_1_out7), .in(undriven), .sel(undriven_3));  // open: en
  Register register_1 (.D(demultiplexer_1_out0), .en(undriven_4), .Q(register_1_q), .clk(undriven_2));  // open: clr
  Register register_2 (.D(demultiplexer_1_out1), .en(undriven_4), .Q(register_2_q), .clk(undriven_2));  // open: clr
  Register register_3 (.D(demultiplexer_1_out2), .en(undriven_4), .Q(register_3_q), .clk(undriven_2));  // open: clr
  Register register_4 (.D(demultiplexer_1_out3), .en(undriven_4), .Q(register_4_q), .clk(undriven_2));  // open: clr
  Register register_5 (.D(demultiplexer_1_out4), .en(undriven_4), .Q(register_5_q), .clk(undriven_2));  // open: clr
  Register register_6 (.D(demultiplexer_1_out5), .en(undriven_4), .Q(register_6_q), .clk(undriven_2));  // open: clr
  Register register_7 (.D(demultiplexer_1_out6), .en(undriven_4), .Q(register_7_q), .clk(undriven_2));  // open: clr
  Register register_8 (.D(demultiplexer_1_out7), .en(undriven_4), .Q(register_8_q), .clk(undriven_2));  // open: clr
  Multiplexer #(.select(3), .width(8)) multiplexer_1 (
    .in0(register_1_q), .in1(register_2_q), .in2(register_3_q), .in3(register_4_q), .in4(register_5_q),
    .in5(register_6_q), .in6(register_7_q), .in7(register_8_q), .out(multiplexer_1_out), .sel(undriven_5));  // open: en
endmodule
