// Logisim project sketch_16x.circ as structural Verilog: 8 circuits, main circuit CPU
module CPU (
  input  in_1
);

  wire alu_1_zero, clk, j, LM, SM, undriven, undriven_2, undriven_3;
  wire [3:0] undriven_4;
  wire [15:0] A, adder_1_out, alu_1_dataout, d2, demultiplexer_1_out0, demultiplexer_1_out1, I,
       multiplexer_1_out, multiplexer_2_out, PC_q, ram_1_dataout, regs_1_data1;

  Clock clock_1 (.out(clk));
  Register #(.width(16)) PC (.D(multiplexer_1_out), .Q(PC_q), .clk(clk), .clr(in_1));  // open: en
  Multiplexer #(.width(16)) multiplexer_1 (.in0(adder_1_out), .in1(A), .out(multiplexer_1_out), .sel(j));  // open: en
  Adder #(.width(16)) adder_1 (.a(16'h1), .b(PC_q), .out(adder_1_out));  // open: cin, cout
  Regs regs_1 (
    .RegSelect(I[7:4]), .RegTelect(I[3:0]), .RedDest(I[11:8]), .DataIn(multiplexer_2_out),
    .Data1(regs_1_data1), .Data2(d2), .str(undriven), .clk(clk), .clr(in_1));
  ROM_part #(.addrWidth(16), .dataWidth(16)) rom_1 (.addr(PC_q), .data(I));  // open: sel
  ALU alu_1 (
    .Data1(regs_1_data1), .Data2(d2), .DataOut(alu_1_dataout), .ALUOp(undriven_4),
    .Immed({4'b0000, I[11:0]}), .Zero(alu_1_zero));
  branch branch_1 (.in_1(undriven_2), .in_2(undriven_3), .in_3(alu_1_zero), .out_4(j));
  Demultiplexer #(.width(16)) demultiplexer_1 (
    .out0(demultiplexer_1_out0), .out1(demultiplexer_1_out1), .in(alu_1_dataout), .sel(LM));  // open: en
  Multiplexer #(.width(16)) multiplexer_2 (
    .in0(demultiplexer_1_out0), .in1(ram_1_dataout), .out(multiplexer_2_out), .sel(LM));  // open: en
  RAM ram_1 (
    .Address(demultiplexer_1_out1), .DataIn(d2), .DataOut(ram_1_dataout), .sw(SM), .clk(clk), .lw(LM),
    .clr(in_1));

  // Other names for the same wires on the sheet: clr = in_1

  // Notes on the sheet:
  //   Data1
  //   Data2
  //   Immed
  //   contents of rom_1 (hex, n*v repeats v):
  //   110a 0 d000
endmodule

module ALU (
  input  [3:0] ALUOp,
  input  [15:0] Data1,
  input  [15:0] Data2,
  input  [15:0] Immed,
  output [15:0] DataOut,
  output Zero
);

  wire and_1_out, and_2_out, comparator_1_gt, comparator_2_gt, not_1_out;
  wire [15:0] adder_1_out, adder_2_out, adder_3_out, bit_extender_1_out, bit_extender_2_out, shifter_1_out,
       shifter_2_out, subtractor_1_out, subtractor_2_out, tag2_1_out_2, tag4_1_out_2, tag4_2_out_2;

  tag4 tag4_1 (.out_2(tag4_1_out_2), .in_1(Immed));
  tag4 tag4_2 (.out_2(tag4_2_out_2), .in_1(Immed));
  tag2 tag2_1 (.in_1(Immed), .out_2(tag2_1_out_2));
  Adder #(.width(16)) adder_1 (.a(Data1), .b(Data2), .out(adder_1_out));  // open: cin, cout
  Adder #(.width(16)) adder_2 (.a(Data1), .b(tag4_1_out_2), .out(adder_2_out));  // open: cin, cout
  Subtractor #(.width(16)) subtractor_1 (.a(Data1), .b(Data2), .out(subtractor_1_out));  // open: bin, bout
  Subtractor #(.width(16)) subtractor_2 (.a(Data1), .b(tag4_2_out_2), .out(subtractor_2_out));  // open: bin, bout
  Shifter #(.width(16)) shifter_1 (.in(Data1), .\dist (Immed[3:0]), .out(shifter_1_out));
  Shifter #(.width(16), .shift("lr")) shifter_2 (.in(Data1), .\dist (Immed[3:0]), .out(shifter_2_out));
  assign bit_extender_1_out = {{15{1'b0}}, comparator_1_gt};  // Bit_Extender bit_extender_1
  Comparator #(.width(16)) comparator_1 (.a(Data1), .b(Data2), .gt(comparator_1_gt));  // open: eq, lt
  assign bit_extender_2_out = {{15{1'b0}}, comparator_2_gt};  // Bit_Extender bit_extender_2
  Comparator #(.width(16)) comparator_2 (.a(Data1), .b(Immed), .gt(comparator_2_gt));  // open: eq, lt
  Adder #(.width(16)) adder_3 (.a(Data1), .b(tag2_1_out_2), .out(adder_3_out));  // open: cin, cout
  Multiplexer #(.select(4), .width(16)) multiplexer_1 (
    .in0(Immed), .in1(adder_1_out), .in2(adder_2_out), .in3(subtractor_1_out), .in4(subtractor_2_out),
    .in5(shifter_1_out), .in6(shifter_2_out), .in7(bit_extender_1_out), .in8(bit_extender_2_out),
    .in9(adder_3_out), .in10(tag2_1_out_2), .in11(tag2_1_out_2), .in12({16{1'b0}}), .in13({16{1'b0}}),
    .in14({16{1'b0}}), .in15({16{1'b0}}), .out(DataOut), .sel(ALUOp));  // open: en
  and and_1 (and_1_out, ALUOp[3], ~ALUOp[2], ALUOp[1], ALUOp[0]);  // AND_Gate
  Multiplexer multiplexer_2 (.in0(and_2_out), .in1(not_1_out), .out(Zero), .sel(and_1_out));  // open: en
  not not_1 (not_1_out, and_2_out);
  and and_2 (and_2_out, DataOut[0], DataOut[1], DataOut[2], DataOut[3], DataOut[4], DataOut[5], DataOut[6], DataOut[7], DataOut[8], DataOut[9], DataOut[10], DataOut[11], DataOut[12], DataOut[13], DataOut[14], DataOut[15]);

  // Notes on the sheet:
  //   1010
  //   1011
endmodule

module Regs (
  input  str,
  input  [3:0] RegSelect,
  input  [3:0] RegTelect,
  input  [3:0] RedDest,
  input  [15:0] DataIn,
  input  clk,
  input  clr,
  output [15:0] Data1,
  output [15:0] Data2
);

  wire demultiplexer_1_out1, demultiplexer_1_out2, demultiplexer_1_out3, demultiplexer_1_out4,
       demultiplexer_1_out5, demultiplexer_1_out6, demultiplexer_1_out7, demultiplexer_1_out8,
       demultiplexer_1_out9, demultiplexer_1_out10, demultiplexer_1_out11, demultiplexer_1_out12,
       demultiplexer_1_out13, demultiplexer_1_out14, demultiplexer_1_out15;
  wire [15:0] demultiplexer_2_out0, demultiplexer_2_out1, demultiplexer_2_out2, demultiplexer_2_out3,
       demultiplexer_2_out4, demultiplexer_2_out5, demultiplexer_2_out6, demultiplexer_2_out7,
       demultiplexer_2_out8, demultiplexer_2_out9, demultiplexer_2_out10, demultiplexer_2_out11,
       demultiplexer_2_out12, demultiplexer_2_out13, demultiplexer_2_out14, demultiplexer_2_out15,
       register_1_q, register_2_q, register_3_q, register_4_q, register_5_q, register_6_q, register_7_q,
       register_8_q, register_9_q, register_10_q, register_11_q, register_12_q, register_13_q, register_14_q,
       register_15_q, register_16_q;

  Demultiplexer #(.select(4)) demultiplexer_1 (
    .out1(demultiplexer_1_out1), .out2(demultiplexer_1_out2), .out3(demultiplexer_1_out3),
    .out4(demultiplexer_1_out4), .out5(demultiplexer_1_out5), .out6(demultiplexer_1_out6),
    .out7(demultiplexer_1_out7), .out8(demultiplexer_1_out8), .out9(demultiplexer_1_out9),
    .out10(demultiplexer_1_out10), .out11(demultiplexer_1_out11), .out12(demultiplexer_1_out12),
    .out13(demultiplexer_1_out13), .out14(demultiplexer_1_out14), .out15(demultiplexer_1_out15), .in(str),
    .sel(RedDest));  // open: out0, en
  Demultiplexer #(.select(4), .width(16)) demultiplexer_2 (
    .out0(demultiplexer_2_out0), .out1(demultiplexer_2_out1), .out2(demultiplexer_2_out2),
    .out3(demultiplexer_2_out3), .out4(demultiplexer_2_out4), .out5(demultiplexer_2_out5),
    .out6(demultiplexer_2_out6), .out7(demultiplexer_2_out7), .out8(demultiplexer_2_out8),
    .out9(demultiplexer_2_out9), .out10(demultiplexer_2_out10), .out11(demultiplexer_2_out11),
    .out12(demultiplexer_2_out12), .out13(demultiplexer_2_out13), .out14(demultiplexer_2_out14),
    .out15(demultiplexer_2_out15), .in(DataIn), .sel(RedDest));  // open: en
  Register #(.width(16)) register_1 (.D(demultiplexer_2_out0), .en(1'b0), .Q(register_1_q), .clk(clk), .clr(clr));
  Register #(.width(16)) register_2 (
    .D(demultiplexer_2_out1), .en(demultiplexer_1_out1), .Q(register_2_q), .clk(clk), .clr(clr));
  Register #(.width(16)) register_3 (
    .D(demultiplexer_2_out2), .en(demultiplexer_1_out2), .Q(register_3_q), .clk(clk), .clr(clr));
  Register #(.width(16)) register_4 (
    .D(demultiplexer_2_out3), .en(demultiplexer_1_out3), .Q(register_4_q), .clk(clk), .clr(clr));
  Register #(.width(16)) register_5 (
    .D(demultiplexer_2_out4), .en(demultiplexer_1_out4), .Q(register_5_q), .clk(clk), .clr(clr));
  Register #(.width(16)) register_6 (
    .D(demultiplexer_2_out5), .en(demultiplexer_1_out5), .Q(register_6_q), .clk(clk), .clr(clr));
  Register #(.width(16)) register_7 (
    .D(demultiplexer_2_out6), .en(demultiplexer_1_out6), .Q(register_7_q), .clk(clk), .clr(clr));
  Register #(.width(16)) register_8 (
    .D(demultiplexer_2_out7), .en(demultiplexer_1_out7), .Q(register_8_q), .clk(clk), .clr(clr));
  Register #(.width(16)) register_9 (
    .D(demultiplexer_2_out8), .en(demultiplexer_1_out8), .Q(register_9_q), .clk(clk), .clr(clr));
  Register #(.width(16)) register_10 (
    .D(demultiplexer_2_out9), .en(demultiplexer_1_out9), .Q(register_10_q), .clk(clk), .clr(clr));
  Register #(.width(16)) register_11 (
    .D(demultiplexer_2_out10), .en(demultiplexer_1_out10), .Q(register_11_q), .clk(clk), .clr(clr));
  Register #(.width(16)) register_12 (
    .D(demultiplexer_2_out11), .en(demultiplexer_1_out11), .Q(register_12_q), .clk(clk), .clr(clr));
  Register #(.width(16)) register_13 (
    .D(demultiplexer_2_out12), .en(demultiplexer_1_out12), .Q(register_13_q), .clk(clk), .clr(clr));
  Register #(.width(16)) register_14 (
    .D(demultiplexer_2_out13), .en(demultiplexer_1_out13), .Q(register_14_q), .clk(clk), .clr(clr));
  Register #(.width(16)) register_15 (
    .D(demultiplexer_2_out14), .en(demultiplexer_1_out14), .Q(register_15_q), .clk(clk), .clr(clr));
  Register #(.width(16)) register_16 (
    .D(demultiplexer_2_out15), .en(demultiplexer_1_out15), .Q(register_16_q), .clk(clk), .clr(clr));
  Multiplexer #(.select(4), .width(16)) multiplexer_1 (
    .in0(register_1_q), .in1(register_2_q), .in2(register_3_q), .in3(register_4_q), .in4(register_5_q),
    .in5(register_6_q), .in6(register_7_q), .in7(register_8_q), .in8(register_9_q), .in9(register_10_q),
    .in10(register_11_q), .in11(register_12_q), .in12(register_13_q), .in13(register_14_q),
    .in14(register_15_q), .in15(register_16_q), .out(Data1), .sel(RegSelect));  // open: en
  Multiplexer #(.select(4), .width(16)) multiplexer_2 (
    .in0(register_1_q), .in1(register_2_q), .in2(register_3_q), .in3(register_4_q), .in4(register_5_q),
    .in5(register_6_q), .in6(register_7_q), .in7(register_8_q), .in8(register_9_q), .in9(register_10_q),
    .in10(register_11_q), .in11(register_12_q), .in12(register_13_q), .in13(register_14_q),
    .in14(register_15_q), .in15(register_16_q), .out(Data2), .sel(RegTelect));  // open: en

  // Other names for the same wires on the sheet: RS[3:0] = RegSelect; RT[3:0] = RegTelect
endmodule

module ROM (
  input  [15:0] Address,
  input  jump,
  input  clk,
  input  clr,
  output [15:0] Instruction
);

  wire [15:0] adder_1_out, multiplexer_1_out, PC_q;

  Multiplexer #(.width(16)) multiplexer_1 (
    .in0(adder_1_out), .in1(Address), .out(multiplexer_1_out), .sel(jump));  // open: en
  Register #(.width(16)) PC (.D(multiplexer_1_out), .Q(PC_q), .clk(clk), .clr(clr));  // open: en
  Adder #(.width(16)) adder_1 (.a(16'h1), .b(PC_q), .out(adder_1_out));  // open: cin, cout
  ROM_part #(.addrWidth(16), .dataWidth(16)) rom_1 (.addr(PC_q), .data(Instruction));  // open: sel

  // Notes on the sheet:
  //   contents of rom_1 (hex, n*v repeats v):
  //   b201 d003 d000
endmodule

// MEM
module RAM (
  input  [15:0] Address,
  input  [15:0] DataIn,
  input  sw,
  input  clk,
  input  lw,
  input  clr,
  output [15:0] DataOut
);

  RAM_part #(.addrWidth(16), .dataWidth(16), .bus("separate")) ram_1 (
    .addr(Address), .din(DataIn), .data(DataOut), .str(sw), .sel(1'b1), .clk(clk), .ld(lw), .clr(clr));
endmodule

// s4
module tag4 (
  input  [15:0] in_1,
  output [15:0] out_2
);

  assign out_2 = {{12{1'b0}}, in_1[3:0]};  // Bit_Extender bit_extender_1
endmodule

// s2
module tag2 (
  input  [15:0] in_1,
  output [15:0] out_2
);

  wire [3:0] bitselector_1_out;
  wire [7:0] undriven;

  BitSelector #(.width(16), .group(4)) bitselector_1 (.in(in_1), .out(bitselector_1_out), .sel(2'b10));
  Shifter #(.width(16), .shift("lr")) shifter_1 (
    .in({4'b0000, bitselector_1_out, undriven}), .\dist (4'b1000), .out(out_2));
endmodule

module branch (
  input  in_1,
  input  in_2,
  input  in_3,
  output out_4
);

  wire and_1_out;

  and and_1 (and_1_out, in_2, ~in_3);  // AND_Gate
  or or_1 (out_4, in_1, and_1_out);
endmodule
